# Fritzing sketch schematic (saved by Fritzing 0.9.3b)

parts:
  Arduino_Nano = Arduino Nano (Rev3.0)
  HC-06 = Bluetooth HC-06
  HX711 = HX711 Weighing Sensor Module
  R1 = Resistor [tolerance=±5% resistance=1k package=THT]
  R2 = Resistor [tolerance=±5% resistance=2.2k package=THT]
  J1 = LOAD_CELL [package=1x03]
  J2 = LOAD_CELL [package=1x03]
  J3 = LOAD_CELL [package=1x03]
  J4 = LOAD_CELL [package=1x03]

nets:
  GND: Arduino_Nano.GND, HC-06.GND, HX711.GND, R2.Pin_0
  N1: Arduino_Nano.D2, HC-06.TXD
  N2: Arduino_Nano.D3, R1.Pin_1
  5V: Arduino_Nano.5V, HX711.VCC
  N3: Arduino_Nano.A1, HX711.DO/RX
  N4: Arduino_Nano.A0, HX711.CK/TX
  3V3: Arduino_Nano.3V3, HC-06.VCC
  N5: HC-06.RXD, R1.Pin_0, R2.Pin_1
  N6: HX711.E+, J1.W
  N7: HX711.E-, J3.W
  N8: HX711.A+, J2.W
  N9: HX711.A-, J4.W
  N10: J1.B, J4.B
  N11: J1.R, J2.R
  N12: J2.B, J3.B
  N13: J3.R, J4.R

notes:
  B W R
  R W B
